# Fritzing sketch two-pots-two-leds (saved by Fritzing 0.9.2b)
breadboards: 1

parts:
  Part1 = Arduino Uno (Rev3)
  100_kΩ = TRIMPOT [package=3386u]
  100_kΩ_2 = TRIMPOT [package=3386u]
  R1 = Resistor [tolerance=±5% resistance=330 package=THT]
  R2 = Resistor [tolerance=±5% resistance=330 package=THT]
  LED1 = LED - 5mm [color="Red (633nm)" package="5 mm [THT]"]
  LED2 = LED - 5mm [color="Red (633nm)" package="5 mm [THT]"]

nets:
  N1: Part1.A0, 100_kΩ.WIPER
  N2: Part1.A1, 100_kΩ_2.WIPER
  N3: Part1.D5_PWM, R2.Pin_0
  N4: Part1.D6_PWM, R1.Pin_0
  N5: Part1.5V, 100_kΩ.CCW, 100_kΩ_2.CCW
  N6: Part1.GND, 100_kΩ.CW, 100_kΩ_2.CW, LED1.cathode, LED2.cathode
  N7: R1.Pin_1, LED1.anode
  N8: R2.Pin_1, LED2.anode
